# Fritzing sketch Watering_Can_Schematic (saved by Fritzing 0.9.5d)
circuit board: 6.88566cm x 5.36311cm

parts:
  Sensor_5________Sensor_4 = Header 12 [package=1x12_machine-pin-header_lock.004]
  Sensor_3________Sensor_2 = Header 12 [package=1x12_machine-pin-header_lock.004]
  Sensor_1________Sensor_0 = Header 12 [package=1x12_machine-pin-header_lock.004]
  Arduino_Uno = Arduino Uno (Rev3)

nets:
  N1: Sensor_5________Sensor_4.1, Sensor_5________Sensor_4.9, Sensor_3________Sensor_2.1, Sensor_3________Sensor_2.9, Sensor_1________Sensor_0.1, Sensor_1________Sensor_0.9, Arduino_Uno.5V
  N2: Sensor_5________Sensor_4.2, Sensor_5________Sensor_4.10, Sensor_3________Sensor_2.2, Sensor_3________Sensor_2.10, Sensor_1________Sensor_0.2, Sensor_1________Sensor_0.10, Arduino_Uno.GND
  N3: Sensor_5________Sensor_4.4, Arduino_Uno.A5/SCL
  N4: Sensor_5________Sensor_4.12, Arduino_Uno.A4/SDA
  N5: Sensor_3________Sensor_2.4, Arduino_Uno.A3
  N6: Sensor_3________Sensor_2.12, Arduino_Uno.A2
  N7: Sensor_1________Sensor_0.4, Arduino_Uno.A1
  N8: Sensor_1________Sensor_0.12, Arduino_Uno.A0
